# Fritzing sketch PiezoButtonController (saved by Fritzing 0.9.3b)
breadboards: 1

parts:
  Part1 = Arduino Uno (Rev3)
  S1 = Pushbutton [package="[THT]"]
  S2 = Pushbutton [package="[THT]"]
  S3 = Pushbutton [package="[THT]"]
  S4 = Pushbutton [package="[THT]"]
  R1 = Resistor [tolerance=±5% resistance=10k package=THT]
  R2 = Resistor [tolerance=±5% resistance=10k package=THT]
  R3 = Resistor [tolerance=±5% resistance=10k package=THT]
  R4 = Resistor [tolerance=±5% resistance=10k package=THT]
  LED1 = LED - 5mm [color="Blue (430nm)" package="5 mm [THT]"]
  R6 = Resistor [tolerance=±5% resistance=220 package=THT]
  R7 = Resistor [tolerance=±5% resistance=220 package=THT]
  R8 = Resistor [tolerance=±5% resistance=220 package=THT]
  LED5 = LED - 5mm [color="Red (633nm)" package="5 mm [THT]"]
  LED6 = LED - 5mm [color="Yellow (585nm)" package="5 mm [THT]"]
  LED7 = LED - 5mm [color="Green (560nm)" package="5 mm [THT]"]
  R9 = Resistor [tolerance=±5% resistance=220 package=THT]
  R10 = Resistor [tolerance=±5% resistance=220 package=THT]
  J1 = Piezo Speaker
  S5 = Pushbutton [package="[THT]"]
  R11 = Resistor [tolerance=±5% resistance=220 package=THT]
  S6 = Pushbutton [package="[THT]"]
  R12 = Resistor [tolerance=±5% resistance=220 package=THT]

nets:
  N1: Part1.D8, Part1.D9_PWM, Part1.D10_PWM/SS, Part1.D11_PWM/MOSI, Part1.GND, S1.Pin_1, S1.Pin_2, S2.Pin_1, S2.Pin_2, S3.Pin_1, S3.Pin_2, S4.Pin_1, S4.Pin_2, R1.Pin_1, R2.Pin_0, R2.Pin_1, R3.Pin_0, R3.Pin_1, R4.Pin_0, R4.Pin_1, LED1.cathode, LED5.cathode, LED6.cathode, LED7.cathode, J1.pin1, R11.Pin_1, R12.Pin_1
  N2: Part1.D13/SCK, R10.Pin_1, J1.pin2
  N3: Part1.D2, S5.Pin_1, S5.Pin_2, R11.Pin_0
  N4: Part1.D3_PWM, R6.Pin_1, LED5.anode
  N5: Part1.D4, R8.Pin_1, LED7.anode
  N6: Part1.D5_PWM, LED1.anode, R7.Pin_1
  N7: Part1.D6_PWM, LED6.anode, R9.Pin_1
  N8: Part1.D7, S6.Pin_1, S6.Pin_2, R12.Pin_0
  N9: Part1.5V, S1.Pin_3, S1.Pin_4, S2.Pin_3, S2.Pin_4, S3.Pin_3, S3.Pin_4, S4.Pin_3, S4.Pin_4, R6.Pin_0, R7.Pin_0, R8.Pin_0, R9.Pin_0, R10.Pin_0, S5.Pin_3, S5.Pin_4, S6.Pin_3, S6.Pin_4
